// Digital circuit main.dig as structural Verilog
module main (
  input  CLOCK
);

  wire CLEAR_out, mod12_1_b0, mod12_1_b1, mod12_1_b2, mod12_1_b3, mod12_1_b4, mod12_1_o, mod60_1_p1,
       mod60_1_p2, mod60_1_p3, mod60_1_p4, mod60_1_p5, mod60_1_p7, mod60_1_p8, mod60_1_p9, mod60_2_p2,
       mod60_2_p3, mod60_2_p4, mod60_2_p5, mod60_2_p7, mod60_2_p9, or_1_out;

  Button CLEAR (.out(CLEAR_out));
  or or_1 (or_1_out, CLEAR_out, mod12_1_o);
  Seven_Seg seven_seg_1 ();  // open: a, b, c, d, e, f, g, dp
  Seven_Seg seven_seg_2 ();  // open: a, b, c, d, e, f, g, dp
  mod12 mod12_1 (
    .CK(mod60_1_p1), .CL(or_1_out), .B0(mod12_1_b0), .B1(mod12_1_b1), .B2(mod12_1_b2), .B3(mod12_1_b3),
    .B4(mod12_1_b4), .O(mod12_1_o));
  decoder decoder_1 (
    .i0(mod12_1_b0), .i1(mod12_1_b1), .i2(mod12_1_b2), .i3(mod12_1_b3), .i4(mod12_1_b4), .i5(1'b0));  // open: o0, o1, o2, o3, o4, o5
  Seven_Seg seven_seg_3 ();  // open: a, b, c, d, e, f, g, dp
  Seven_Seg seven_seg_4 ();  // open: a, b, c, d, e, f, g, dp
  // mod60 mod60_1: pin names not known; wires that end beside it: mod60_1_p1, mod60_1_p2, mod60_1_p3, mod60_1_p4, mod60_1_p5, or_1_out, mod60_1_p7, mod60_1_p8, mod60_1_p9
  decoder decoder_2 (
    .i0(mod60_1_p9), .i1(mod60_1_p7), .i2(mod60_1_p5), .i3(mod60_1_p4), .i4(mod60_1_p3), .i5(mod60_1_p2));  // open: o0, o1, o2, o3, o4, o5
  Seven_Seg seven_seg_5 ();  // open: a, b, c, d, e, f, g, dp
  Seven_Seg seven_seg_6 ();  // open: a, b, c, d, e, f, g, dp
  // mod60 mod60_2: pin names not known; wires that end beside it: mod60_1_p8, mod60_2_p2, mod60_2_p3, mod60_2_p4, mod60_2_p5, or_1_out, mod60_2_p7, CLOCK, mod60_2_p9
  decoder decoder_3 (
    .i0(mod60_2_p9), .i1(mod60_2_p7), .i2(mod60_2_p5), .i3(mod60_2_p4), .i4(mod60_2_p3), .i5(mod60_2_p2));  // open: o0, o1, o2, o3, o4, o5
endmodule
